# Fritzing sketch control_unit (saved by Fritzing 0.9.4)

parts:
  WeMos_D1_Mini1 = WeMos D1 Mini
  Component1 = RS485_XY-017 [part_number=XY-017]
  J1 = Piezo Speaker
  S1 = Round Pushbutton
  Bauteil1 = Adafruit 1.44 inch TFT Breakout [part_number="Adafruit #2088"]

nets:
  3V3: WeMos_D1_Mini1.3V3, Component1.VCC, Bauteil1.VIN
  N1: WeMos_D1_Mini1.5V, J1.pin2
  N2: WeMos_D1_Mini1.D0, Bauteil1.LITE
  N3: WeMos_D1_Mini1.D1, Component1.RXD
  N4: WeMos_D1_Mini1.D2, S1.leg0
  N5: WeMos_D1_Mini1.D3, Bauteil1.TFTDC
  N6: WeMos_D1_Mini1.D4, Component1.TXD
  N7: WeMos_D1_Mini1.D5, Bauteil1.SCK
  N8: WeMos_D1_Mini1.D6, J1.pin1
  N9: WeMos_D1_Mini1.D7, Bauteil1.MOSI
  N10: WeMos_D1_Mini1.D8, Bauteil1.TFTCS
  GND: WeMos_D1_Mini1.G, Component1.GND, S1.leg1, Bauteil1.GND

custom parts:
  RS485_XY-017: Commercially available RS485 to RS232 TTL Module
  Adafruit 1.44 inch TFT Breakout: This lovely little display breakout is the best way to add a small, colorful and bright display to any project. Since the display uses 4-wire SPI to communicate and has its own pixel-addressable frame buffer, it can be used with every kind of microcontroller. Even a very small one with low memory and few pins available! The 1.44" display has 128x128 color pixels. Unlike the low cost "Nokia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
