# Fritzing sketch sensor_unit (saved by Fritzing 0.9.4)

parts:
  WeMos_D1_Mini2 = WeMos D1 Mini
  Bauteil2 = Adafruit BME280
  Bauteil5 = Adafruit BME280
  Bauteil6 = Adafruit BME280
  Bauteil7 = Adafruit BME280
  Bauteil8 = Adafruit BME280
  Bauteil9 = Adafruit BME280
  Bauteil10 = Adafruit TCA9548A
  Component1 = RS485_XY-017 [part_number=XY-017]

nets:
  VIN: WeMos_D1_Mini2.3V3, Bauteil2.VIN, Bauteil5.VIN, Bauteil6.VIN, Bauteil7.VIN, Bauteil8.VIN, Bauteil9.VIN, Bauteil10.VCC, Component1.VCC
  N1: WeMos_D1_Mini2.D1, Bauteil10.INPUTSCL
  N2: WeMos_D1_Mini2.D2, Bauteil10.INPUTSDA
  N3: WeMos_D1_Mini2.D3, Component1.RXD
  N4: WeMos_D1_Mini2.D6, Component1.TXD
  GND: WeMos_D1_Mini2.G, Bauteil2.GND, Bauteil2.SDO/ADR, Bauteil5.GND, Bauteil6.GND, Bauteil7.GND, Bauteil7.SDO/ADR, Bauteil8.GND, Bauteil9.GND, Bauteil9.SDO/ADR, Bauteil10.GND, Component1.GND
  N5: Bauteil2.SCK/SCL, Bauteil6.SCK/SCL, Bauteil10.1SCL
  N6: Bauteil2.SDI/SDA, Bauteil6.SDI/SDA, Bauteil10.1SDA
  N7: Bauteil5.SCK/SCL, Bauteil7.SCK/SCL, Bauteil10.0SCL
  N8: Bauteil5.SDI/SDA, Bauteil7.SDI/SDA, Bauteil10.0SDA
  N9: Bauteil8.SCK/SCL, Bauteil9.SCK/SCL, Bauteil10.2SCL
  N10: Bauteil8.SDI/SDA, Bauteil9.SDI/SDA, Bauteil10.2SDA

custom parts:
  Adafruit BME280: Bosch has stepped up their game with their new BME280 sensor, an environmental sensor with temperature, barometric pressure and humidity! This sensor is great for all sorts of weather/environmental sensing and can even be used in both I2C and SPI! This precision sensor from Bosch is the best low-cost sensing solution for measuring humidity with ±3% accuracy, barometric pressure with ±1 hPa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
  Adafruit TCA9548A: You just found the perfect I2C sensor, and you want to wire up two or three or more of them to your Arduino when you realize "Uh oh, this chip has a fixed I2C address, and from what I know about I2C, you cannot have two devices with the same address on the same SDA/SCL pins!" Are you out of luck? You would be, if you didn't have this ultra-cool TCA9548A 1-to-8 I2C multiplexer! Finally, a way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
  RS485_XY-017: Commercially available RS485 to RS232 TTL Module
